// Logisim project teste_bit-sinal.circ as structural Verilog: 1 circuit, main circuit main
module main (
  input  Sinal_1,
  input  Sinal_2,
  input  Resultado_Bit_Sinal,
  output out_4
);

  wire and_1_out;

  and and_1 (and_1_out, Sinal_1, Sinal_2);
  xor xor_1 (out_4, Resultado_Bit_Sinal, and_1_out);
endmodule
